# Fritzing sketch Circuit (saved by Fritzing 0.9.2b)
breadboards: 1

parts:
  DHT22 = Humidity and Temperature Sensor RHT03
  BMP280 = Barometric Pressure Sensor - BMP085 Breakout
  Photoresistor = PHOTOCELL [package=photocell]
  R1 = Resistor [tolerance=±5% resistance=10k package="1206 [SMD]"]
  V1 = DC Power [voltage=3.3V]
  3V3 = Header 1 [package=1x01_offset]
  D1 = Header 1 [package=1x01_offset]
  D2 = Header 1 [package=1x01_offset]
  D3 = Header 1 [package=1x01_offset]
  A0 = Header 1 [package=1x01_offset]
  Jumper/Switch = SWITCH-MOMENTARY-2 [package=tactile-pth]
  D5 = Header 1 [package=1x01_offset]
  GND = Header 1 [package=1x01_offset]

nets:
  VCC: DHT22.Vcc, BMP280.VCC, V1.V+, 3V3.1
  N1: DHT22.Data-signal, D3.1
  GND: DHT22.GND_2, BMP280.GND, R1.Pin_0, V1.V-, Jumper/Switch.2, GND.1
  N2: BMP280.SCL, D1.1
  N3: BMP280.SDA, D2.1
  N4: Photoresistor.P$1, A0.1
  N5: Photoresistor.P$2, R1.Pin_1
  N6: Jumper/Switch.1, D5.1
